// Logisim project mips.circ as structural Verilog
module main (
  input  in_1
);

  wire clock_1_out, e_m_1_out_10, execute_1_we, m_w_1_out_10, memory_1_weo, not_1_out;
  wire [4:0] d_e_1_out_11, d_e_1_out_12, decode_1_rd, decode_1_shamt, e_m_1_out_9, execute_1_rdo,
       m_w_1_out_9, memory_1_rdo;
  wire [6:0] d_e_1_out_13, decode_1_fcn;
  wire [31:0] d_e_1_out_9, d_e_1_out_10, d_e_1_out_14, decode_1_a, decode_1_b, decode_1_imm, e_m_1_out_7,
       e_m_1_out_8, execute_1_bfwd, execute_1_d, m_w_1_out_7, memory_1_do, memory_1_m, mipsprogramrom_1_p2,
       pc_1_pc, register_1_q;

  Clock clock_1 (.out(clock_1_out));
  pc pc_1 (.clk(clock_1_out), .en(in_1), .pc(pc_1_pc));
  Register #(.width(32)) register_1 (
    .D(mipsprogramrom_1_p2), .en(in_1), .clk(clock_1_out), .Q(register_1_q), .clr(not_1_out));
  // MIPSProgramROM mipsprogramrom_1: pin names not known; wires that end beside it: pc_1_pc, mipsprogramrom_1_p2
  not not_1 (not_1_out, in_1);
  decode decode_1 (
    .W(m_w_1_out_7), .clk(clock_1_out), .wE(m_w_1_out_10), .rW(m_w_1_out_9), .Inst(register_1_q),
    .A(decode_1_a), .B(decode_1_b), .rd(decode_1_rd), .shamt(decode_1_shamt), .fcn(decode_1_fcn),
    .imm(decode_1_imm));
  d_e d_e_1 (
    .out_11(d_e_1_out_11), .clk(clock_1_out), .out_10(d_e_1_out_10), .en(in_1), .out_9(d_e_1_out_9),
    .A(decode_1_a), .imm(decode_1_imm), .B(decode_1_b), .fcn(decode_1_fcn), .rd(decode_1_rd),
    .shamt(decode_1_shamt), .out_12(d_e_1_out_12), .out_13(d_e_1_out_13), .out_14(d_e_1_out_14));
  execute execute_1 (
    .A(d_e_1_out_9), .B(d_e_1_out_10), .rd(d_e_1_out_11), .shamt(d_e_1_out_12), .fcn(d_e_1_out_13),
    .imm(d_e_1_out_14), .D(execute_1_d), .Bfwd(execute_1_bfwd), .rdo(execute_1_rdo), .we(execute_1_we));
  e_m e_m_1 (
    .clk(clock_1_out), .out_8(e_m_1_out_8), .en(in_1), .out_7(e_m_1_out_7), .D(execute_1_d),
    .we(execute_1_we), .B(execute_1_bfwd), .rd(execute_1_rdo), .out_9(e_m_1_out_9), .out_10(e_m_1_out_10));
  memory memory_1 (
    .D(e_m_1_out_7), .B(e_m_1_out_8), .rd(e_m_1_out_9), .we(e_m_1_out_10), .Do(memory_1_do), .M(memory_1_m),
    .rdo(memory_1_rdo), .weo(memory_1_weo));
  m_w m_w_1 (
    .clk(clock_1_out), .en(in_1), .out_7(m_w_1_out_7), .D(memory_1_do), .we(memory_1_weo), .M(memory_1_m),
    .rd(memory_1_rdo), .out_9(m_w_1_out_9), .out_10(m_w_1_out_10));  // open: out_8

  // Notes on the sheet:
  //   contents of mipsprogramrom_1 (hex, n*v repeats v):
  //   ANDI  $3, $3, 0x0 # clear reg 3 ANDI  $4, $4, 0x0 # clear reg 4 ANDI  $5, $5, 0x0 # clear reg 5 ANDI
  //   $6, $6, 0x0 # clear reg 6 ANDI  $7, $7, 0x0 # clear reg 7 ADDIU $2, $0, 0x20 NOP NOP SLTI  $5, $2,
  //   0x22 # 0x1 SLTI  $6, $2, 0x19 # 0x0 ORI   $3, $2, 0xf0 XORI  $4, $2, 0xff MOVN  $7, $2, $5 # r7 =
  //   0x20 MOVN  $8, $2, $6 # r8 = 0x0
endmodule

module pc (
  input  clk,
  input  en,
  output [31:0] pc
);

  wire not_1_out;
  wire [31:2] incrementer_1_p2;

  Register #(.width(32)) register_1 (.D({incrementer_1_p2, pc[1:0]}), .en(en), .clk(clk), .Q(pc), .clr(not_1_out));
  not not_1 (not_1_out, en);
  // Incrementer #(.width(30)) incrementer_1: pin names not known; wires that end beside it: pc[31:2], incrementer_1_p2
endmodule

module decode (
  input  [31:0] W,
  input  clk,
  input  wE,
  input  [4:0] rW,
  input  [31:0] Inst,
  output [31:0] A,
  output [31:0] B,
  output [4:0] rd,
  output [4:0] shamt,
  output [6:0] fcn,
  output [31:0] imm
);

  wire not_1_out;
  wire [31:0] bit_extender_1_out, bit_extender_2_out, bit_extender_3_out, multiplexer_3_out;

  not not_1 (not_1_out, clk);
  // RegisterFile registerfile_1: pin names not known; wires that end beside it: W, not_1_out, wE, rW, Inst[25:21], Inst[20:16], A, B
  assign bit_extender_1_out = {{27{1'b0}}, Inst[10:6]};  // Bit_Extender bit_extender_1
  Multiplexer #(.width(5), .enable("false")) multiplexer_1 (
    .in0(Inst[15:11]), .in1(Inst[20:16]), .out(rd), .sel(Inst[29]));
  assign bit_extender_2_out = {{16{Inst[15]}}, Inst[15:0]};  // Bit_Extender bit_extender_2
  assign bit_extender_3_out = {{16{1'b0}}, Inst[15:0]};  // Bit_Extender bit_extender_3
  Multiplexer #(.width(6), .enable("false")) multiplexer_2 (
    .in0(Inst[5:0]), .in1(Inst[31:26]), .out(fcn[5:0]), .sel(fcn[6]));
  or or_1 (fcn[6], Inst[26], Inst[27], Inst[28], Inst[29], Inst[30], Inst[31]);
  Multiplexer #(.width(32), .enable("false")) multiplexer_3 (
    .in0(bit_extender_2_out), .in1(bit_extender_3_out), .out(multiplexer_3_out), .sel(Inst[28]));
  Multiplexer #(.width(32), .enable("false")) multiplexer_4 (
    .in0(multiplexer_3_out), .in1(bit_extender_1_out), .out(imm), .sel(Inst[3]));

  assign shamt = Inst[10:6];
endmodule

module d_e (
  input  clk,
  input  en,
  input  [31:0] A,
  input  [31:0] B,
  input  [4:0] rd,
  input  [4:0] shamt,
  input  [6:0] fcn,
  input  [31:0] imm,
  output [31:0] out_9,
  output [31:0] out_10,
  output [4:0] out_11,
  output [4:0] out_12,
  output [6:0] out_13,
  output [31:0] out_14
);

  wire not_1_out;

  not not_1 (not_1_out, en);
  Register #(.width(32)) register_1 (.D(A), .en(en), .clk(clk), .Q(out_9), .clr(not_1_out));
  Register #(.width(32)) register_2 (.D(B), .en(en), .clk(clk), .Q(out_10), .clr(not_1_out));
  Register #(.width(5)) register_3 (.D(rd), .en(en), .clk(clk), .Q(out_11), .clr(not_1_out));
  Register #(.width(5)) register_4 (.D(shamt), .en(en), .clk(clk), .Q(out_12), .clr(not_1_out));
  Register #(.width(7)) register_5 (.D(fcn), .en(en), .clk(clk), .Q(out_13), .clr(not_1_out));
  Register #(.width(32)) register_6 (.D(imm), .en(en), .clk(clk), .Q(out_14), .clr(not_1_out));
endmodule

module execute_old (
  input  [31:0] A,
  input  [31:0] B,
  input  [4:0] rd,
  input  [4:0] shamt,
  input  [6:0] fcn,
  input  [31:0] imm,
  output [31:0] C,
  output [31:0] Bf,
  output [4:0] rdo,
  output we
);

  wire and_1_out, and_2_out, and_3_out, and_4_out, comparator_1_eq, comparator_1_lt, comparator_2_eq,
       comparator_2_lt, multiplexer_2_out, or_1_out, or_2_out, xor_1_out;
  wire [31:0] bit_extender_1_out, mips_alu_1_p5, multiplexer_1_out, multiplexer_3_out, multiplexer_4_out;

  or or_1 (or_1_out, fcn[3], fcn[6]);
  Multiplexer #(.width(32), .enable("false")) multiplexer_1 (
    .in0(B), .in1(imm), .out(multiplexer_1_out), .sel(or_1_out));
  and and_1 (and_1_out, fcn[3], ~fcn[6], ~fcn[2]);  // AND_Gate
  Comparator #(.width(32)) comparator_1 (
    .a(A), .b(multiplexer_1_out), .eq(comparator_1_eq), .lt(comparator_1_lt));  // open: gt
  Comparator #(.width(32), .mode("unsigned")) comparator_2 (
    .a(A), .b(multiplexer_1_out), .eq(comparator_2_eq), .lt(comparator_2_lt));  // open: gt
  // Mips_ALU mips_alu_1: pin names not known; wires that end beside it: A, multiplexer_1_out, {fcn[2:0], 1'b0}, shamt, mips_alu_1_p5
  Multiplexer #(.enable("false")) multiplexer_2 (
    .in0(comparator_1_lt), .in1(comparator_2_lt), .out(multiplexer_2_out), .sel(fcn[0]));
  assign bit_extender_1_out = {{31{1'b0}}, multiplexer_2_out};  // Bit_Extender bit_extender_1
  Multiplexer #(.width(32), .enable("false")) multiplexer_3 (
    .in0(mips_alu_1_p5), .in1(bit_extender_1_out), .out(multiplexer_3_out), .sel(and_1_out));
  and and_2 (and_2_out, fcn[2], fcn[1], fcn[0], fcn[3]);
  or or_2 (or_2_out, comparator_1_eq, comparator_2_eq);
  xor xor_1 (xor_1_out, or_2_out, fcn[0]);
  Multiplexer #(.width(32), .enable("false")) multiplexer_4 (
    .in0(multiplexer_3_out), .in1({imm[15:0], imm[31:16]}), .out(multiplexer_4_out), .sel(and_2_out));
  and and_3 (and_3_out, ~fcn[5], xor_1_out);  // AND_Gate
  Multiplexer #(.width(32), .enable("false")) multiplexer_5 (
    .in0(multiplexer_4_out), .in1(B), .out(C), .sel(and_3_out));
  and and_4 (and_4_out, ~and_3_out, and_1_out, ~fcn[5]);  // AND_Gate
  xor xor_2 (we, and_4_out, 1'b1);

  assign rdo = rd;
endmodule

module e_m (
  input  clk,
  input  en,
  input  [31:0] D,
  input  [31:0] B,
  input  [4:0] rd,
  input  we,
  output [31:0] out_7,
  output [31:0] out_8,
  output [4:0] out_9,
  output out_10
);

  wire not_1_out;

  not not_1 (not_1_out, en);
  Register #(.width(32)) register_1 (.D(D), .en(en), .clk(clk), .Q(out_7), .clr(not_1_out));
  Register #(.width(32)) register_2 (.D(B), .en(en), .clk(clk), .Q(out_8), .clr(not_1_out));
  Register #(.width(5)) register_3 (.D(rd), .en(en), .clk(clk), .Q(out_9), .clr(not_1_out));
  Register #(.width(1)) register_4 (.D(we), .en(en), .clk(clk), .Q(out_10), .clr(not_1_out));
endmodule

module memory (
  input  [31:0] D,
  input  [31:0] B,
  input  [4:0] rd,
  input  we,
  output [31:0] Do,
  output [31:0] M,
  output [4:0] rdo,
  output weo
);


  assign Do = D;
  assign M = B;
  assign rdo = rd;
  assign weo = we;
endmodule

module m_w (
  input  clk,
  input  en,
  input  [31:0] D,
  input  [31:0] M,
  input  [4:0] rd,
  input  we,
  output [31:0] out_7,
  output [31:0] out_8,
  output [4:0] out_9,
  output out_10
);

  wire not_1_out;

  not not_1 (not_1_out, en);
  Register #(.width(32)) register_1 (.D(D), .en(en), .clk(clk), .Q(out_7), .clr(not_1_out));
  Register #(.width(32)) register_2 (.D(M), .en(en), .clk(clk), .Q(out_8), .clr(not_1_out));
  Register #(.width(5)) register_3 (.D(rd), .en(en), .clk(clk), .Q(out_9), .clr(not_1_out));
  Register #(.width(1)) register_4 (.D(we), .en(en), .clk(clk), .Q(out_10), .clr(not_1_out));
endmodule

module execute (
  input  [31:0] A,
  input  [31:0] B,
  input  [4:0] rd,
  input  [4:0] shamt,
  input  [6:0] fcn,
  input  [31:0] imm,
  output [31:0] D,
  output [31:0] Bfwd,
  output [4:0] rdo,
  output we
);

  wire comp_1_eq, comp_1_lt, parser_1_bori, parser_1_lui, parser_1_mov, parser_1_stl, parser_1_var;
  wire [3:0] parser_1_op;
  wire [4:0] multiplexer_3_out;
  wire [31:0] bit_extender_1_out, bit_extender_2_out, mips_alu_1_p1, mips_alu_1_p6, multiplexer_1_out,
       multiplexer_2_out, multiplexer_4_out, multiplexer_5_out;

  Multiplexer #(.width(32), .enable("false")) multiplexer_1 (
    .in0(A), .in1(imm), .out(multiplexer_1_out), .sel(parser_1_mov));
  Multiplexer #(.width(32), .enable("false")) multiplexer_2 (
    .in0(B), .in1(imm), .out(multiplexer_2_out), .sel(parser_1_bori));
  parser parser_1 (
    .ctrl(fcn), .BorI(parser_1_bori), .op(parser_1_op), .stl(parser_1_stl), .lui(parser_1_lui),
    .mov(parser_1_mov), .\var (parser_1_var));
  Multiplexer #(.width(5), .enable("false")) multiplexer_3 (
    .in0(shamt), .in1(mips_alu_1_p1[4:0]), .out(multiplexer_3_out), .sel(parser_1_var));
  assign bit_extender_1_out = {{16{1'b0}}, imm[15:0]};  // Bit_Extender bit_extender_1
  comp comp_1 (.A(multiplexer_1_out), .B(multiplexer_2_out), .ctrl(fcn), .lt(comp_1_lt), .eq(comp_1_eq));
  // Mips_ALU mips_alu_1: pin names not known; wires that end beside it: mips_alu_1_p1, A, multiplexer_2_out, parser_1_op, multiplexer_3_out, mips_alu_1_p6
  assign bit_extender_2_out = {{31{1'b0}}, comp_1_lt};  // Bit_Extender bit_extender_2
  Multiplexer #(.width(32), .enable("false")) multiplexer_4 (
    .in0(mips_alu_1_p6), .in1({bit_extender_1_out[15:0], bit_extender_1_out[31:16]}),
    .out(multiplexer_4_out), .sel(parser_1_lui));
  Multiplexer #(.width(32), .enable("false")) multiplexer_5 (
    .in0(bit_extender_2_out), .in1(A), .out(multiplexer_5_out), .sel(parser_1_mov));
  Multiplexer #(.width(32), .enable("false")) multiplexer_6 (
    .in0(multiplexer_4_out), .in1(multiplexer_5_out), .out(D), .sel(parser_1_stl));
  or or_1 (we, comp_1_eq, ~parser_1_mov);  // OR_Gate

  assign Bfwd = {32{1'b0}};
  assign rdo = rd;

  // Notes on the sheet:
  //   16 bit shifter
endmodule

module comp (
  input  [31:0] A,
  input  [31:0] B,
  input  [6:0] ctrl,
  output lt,
  output eq
);

  wire comparator_1_eq, comparator_1_lt, comparator_2_eq, comparator_2_lt, or_1_out;

  Comparator #(.width(32)) comparator_1 (.a(A), .b(B), .eq(comparator_1_eq), .lt(comparator_1_lt));  // open: gt
  Comparator #(.width(32), .mode("unsigned")) comparator_2 (
    .a(A), .b(B), .eq(comparator_2_eq), .lt(comparator_2_lt));  // open: gt
  Multiplexer #(.enable("false")) multiplexer_1 (.in0(comparator_1_lt), .in1(comparator_2_lt), .out(lt), .sel(ctrl[0]));
  or or_1 (or_1_out, comparator_1_eq, comparator_2_eq);
  xor xor_1 (eq, or_1_out, ctrl[0]);

  // Notes on the sheet:
  //   signed
  //   unsigned
  //   inv
endmodule

module parser (
  input  [6:0] ctrl,
  output BorI,
  output [3:0] op,
  output stl,
  output lui,
  output mov,
  output \var 
);

  wire and_1_out;
  wire [1:0] xor_1_out;

  and and_1 (and_1_out, ctrl[3], ~ctrl[5]);  // AND_Gate
  and and_2 (xor_1_out[0], ~ctrl[5], ~ctrl[6], ctrl[0]);  // AND_Gate
  xor xor_1 (xor_1_out[1], xor_1_out[0], ctrl[0]);
  and and_3 (stl, ctrl[1], ~ctrl[2], ctrl[3]);  // AND_Gate
  and and_4 (lui, ctrl[0], ctrl[1], ctrl[2], ctrl[3]);
  and and_5 (mov, stl, ~ctrl[5], ~ctrl[6]);  // AND_Gate
  and and_6 (\var , ~ctrl[5], ctrl[2]);  // AND_Gate
  and and_7 (BorI, and_1_out, ~mov);  // AND_Gate
  Multiplexer #(.width(4), .enable("false")) multiplexer_1 (
    .in0({ctrl[2:1], xor_1_out}), .in1({ctrl[3], ctrl[1], ctrl[3], xor_1_out[0]}), .out(op), .sel(\var ));
endmodule
